# Fritzing sketch papatronica (saved by Fritzing 0.9.3b)

parts:
  Part1 = InvenSense MPU6050
  U1 = LIPO-110mAh [package=lipo-110]
  U3 = ESP32-38PinWide [part_number=ESP32-38PinWide]

nets:
  N1: Part1.VCC, U1.+, U3.3.3
  GND: Part1.GND, U1.-, U3.GND
  N2: Part1.SCL, U3.GPIO16
  N3: Part1.SDA, U3.GPIO17

custom parts:
  ESP32-38PinWide: Generic 38-Pin ESP32 with wide format (only access to one side of pins on a breadboard) based on Stephen Lilley's HiLetgo ESP-WROOM-32 ESP32 ESP-32S Development Board.
